// Logisim project riscv.circ as structural Verilog: 9 circuits, main circuit RISCV32
module RISCV32 (
);

  wire and_2_out, and_3_out, bypass_black_box_1_p3, clk, comparator_black_box_1_p4,
       comparator_black_box_1_p5, DE_EX_branch_q, DE_EX_eq_q, DE_EX_JALR_q, DE_EX_posRel_q, DE_EX_regWE_q,
       DE_EX_set_q, DE_EX_shiftreg_q, DE_EX_useImm_q, DE_EX_usePCasA_q, decode_1_branch, decode_1_eq,
       decode_1_jalr, decode_1_jump, decode_1_lb, decode_1_load, decode_1_posrel, decode_1_regwe,
       decode_1_set, decode_1_setsign, decode_1_shiftbyregval, decode_1_store, decode_1_useimm,
       decode_1_usepcasa, decode_1_word_op, jump_q, lb_DX_q, lb_XM_q, LOAD_DX_q, Load_MW_q, Load_XM_q,
       multiplexer_4_out, multiplexer_5_out, multiplexer_7_out, not_1_out, not_2_out, not_3_out, not_4_out,
       not_5_out, not_6_out, not_7_out, or_1_out, registerfile_1_p3, set_signed_q, stall, store_DX_q,
       store_XM_q, word_op_DX_q, word_op_XM_q, xnor_1_out;
  wire [1:0] bypass_black_box_1_p7, bypass_black_box_1_p8;
  wire [3:0] DE_EX_ALUop_q, decode_1_aluop;
  wire [4:0] bit_extender_1_out, bypass_black_box_1_p4, DE_EX_rd_q, decode_1_rd, decode_1_rs1, decode_1_rs2,
       multiplexer_3_out, registerfile_1_p4, rs1_q, rs2_q;
  wire [31:0] and_1_out, bit_extender_2_out, DE_EX_A_q, DE_EX_B_q, DE_EX_imm_q, DE_EX_PC_q, DE_EX_PCn4_q,
       decode_1_imm, decode_1_zeroouta, EX_M_B_q, EX_M_Result_q, execute_1_result, flush_1_nop,
       IF_DE_instr_q, increment_pc_1_out_2, M_W_Data_q, M_W_Result_q, memory_1_d_out, multiplexer_1_out,
       multiplexer_2_out, multiplexer_6_out, multiplexer_8_out, multiplexer_9_out, mux3to1_1_out_5,
       mux3to1_2_out_5, PC_q, PCn4_q, register_1_q, registerfile_1_p1, registerfile_1_p7, registerfile_1_p8,
       risc_vprogramrom_1_p2;

  or or_1 (or_1_out, and_3_out, jump_q);
  Clock clock_1 (.out(clk));
  not not_1 (not_1_out, stall);
  Multiplexer #(.width(32), .enable("false")) multiplexer_1 (
    .in0(increment_pc_1_out_2), .in1(execute_1_result), .out(multiplexer_1_out), .sel(or_1_out));
  Register #(.width(32)) register_1 (.D(multiplexer_1_out), .en(not_1_out), .clk(clk), .Q(register_1_q));  // open: clr
  Flush flush_1 (.jump(or_1_out), .nop(flush_1_nop));
  not not_2 (not_2_out, stall);
  Increment_PC increment_pc_1 (.in_1(register_1_q), .out_2(increment_pc_1_out_2));
  Register #(.width(32)) PCn4 (.D(increment_pc_1_out_2), .en(not_1_out), .clk(clk), .Q(PCn4_q));  // open: clr
  // RISC_VProgramROM risc_vprogramrom_1: pin names not known; wires that end beside it: register_1_q, risc_vprogramrom_1_p2
  Register #(.width(32)) PC (.D(register_1_q), .en(not_2_out), .clk(clk), .Q(PC_q));  // open: clr
  Multiplexer #(.width(32), .enable("false")) multiplexer_2 (
    .in0(risc_vprogramrom_1_p2), .in1(flush_1_nop), .out(multiplexer_2_out), .sel(or_1_out));
  Register #(.width(32)) IF_DE_instr (
    .D(multiplexer_2_out), .en(not_2_out), .clk(clk), .Q(IF_DE_instr_q));  // open: clr
  not not_3 (not_3_out, clk);
  Decode decode_1 (
    .instr(IF_DE_instr_q), .nop(flush_1_nop), .zap(or_1_out), .stall(stall), .rs1(decode_1_rs1),
    .rs2(decode_1_rs2), .rd(decode_1_rd), .imm(decode_1_imm), .useImm(decode_1_useimm),
    .ALUop(decode_1_aluop), .regWE(decode_1_regwe), .set(decode_1_set),
    .shiftbyregval(decode_1_shiftbyregval), .setsign(decode_1_setsign), .UsePCasA(decode_1_usepcasa),
    .ZeroOutA(decode_1_zeroouta), .load(decode_1_load), .branch(decode_1_branch), .JALR(decode_1_jalr),
    .eq(decode_1_eq), .posRel(decode_1_posrel), .jump(decode_1_jump), .store(decode_1_store),
    .word_op(decode_1_word_op), .lb(decode_1_lb));
  // RegisterFile registerfile_1: pin names not known; wires that end beside it: registerfile_1_p1, not_3_out, registerfile_1_p3, registerfile_1_p4, decode_1_rs1, decode_1_rs2, registerfile_1_p7, registerfile_1_p8
  assign and_1_out = registerfile_1_p7 & decode_1_zeroouta;  // AND_Gate and_1, 32 bits wide
  assign bit_extender_1_out = {{4{1'b0}}, not_4_out};  // Bit_Extender bit_extender_1
  not not_4 (not_4_out, stall);
  LoadUseDetection loadusedetection_1 (
    .rs1_FD(decode_1_rs1), .rs2_FD(decode_1_rs2), .rd_DX(DE_EX_rd_q), .load_DX(LOAD_DX_q), .stall(stall));
  Multiplexer #(.width(5), .enable("false")) multiplexer_3 (
    .in0(decode_1_rd), .in1(bit_extender_1_out), .out(multiplexer_3_out), .sel(stall));
  not not_5 (not_5_out, stall);
  not not_6 (not_6_out, stall);
  Multiplexer #(.enable("false")) multiplexer_4 (
    .in0(decode_1_regwe), .in1(not_5_out), .out(multiplexer_4_out), .sel(stall));
  Multiplexer #(.enable("false")) multiplexer_5 (
    .in0(decode_1_store), .in1(not_6_out), .out(multiplexer_5_out), .sel(stall));
  Register #(.width(32)) DE_EX_A (.D(and_1_out), .clk(clk), .Q(DE_EX_A_q));  // open: en, clr
  Register #(.width(32)) DE_EX_B (.D(registerfile_1_p8), .clk(clk), .Q(DE_EX_B_q));  // open: en, clr
  Register #(.width(5)) rs1 (.D(decode_1_rs1), .clk(clk), .Q(rs1_q));  // open: en, clr
  Register #(.width(5)) rs2 (.D(decode_1_rs2), .clk(clk), .Q(rs2_q));  // open: en, clr
  Register #(.width(5)) DE_EX_rd (.D(multiplexer_3_out), .clk(clk), .Q(DE_EX_rd_q));  // open: en, clr
  Register #(.width(32)) DE_EX_imm (.D(decode_1_imm), .clk(clk), .Q(DE_EX_imm_q));  // open: en, clr
  Register #(.width(1)) DE_EX_useImm (.D(decode_1_useimm), .clk(clk), .Q(DE_EX_useImm_q));  // open: en, clr
  Register #(.width(4)) DE_EX_ALUop (.D(decode_1_aluop), .clk(clk), .Q(DE_EX_ALUop_q));  // open: en, clr
  Register #(.width(1)) DE_EX_regWE (.D(multiplexer_4_out), .clk(clk), .Q(DE_EX_regWE_q));  // open: en, clr
  Register #(.width(1)) DE_EX_set (.D(decode_1_set), .clk(clk), .Q(DE_EX_set_q));  // open: en, clr
  Register #(.width(1)) DE_EX_shiftreg (.D(decode_1_shiftbyregval), .clk(clk), .Q(DE_EX_shiftreg_q));  // open: en, clr
  Register #(.width(1)) set_signed (.D(decode_1_setsign), .clk(clk), .Q(set_signed_q));  // open: en, clr
  Register #(.width(1)) DE_EX_usePCasA (.D(decode_1_usepcasa), .clk(clk), .Q(DE_EX_usePCasA_q));  // open: en, clr
  Register #(.width(1)) LOAD_DX (.D(decode_1_load), .clk(clk), .Q(LOAD_DX_q));  // open: en, clr
  Register #(.width(1)) DE_EX_branch (.D(decode_1_branch), .clk(clk), .Q(DE_EX_branch_q));  // open: en, clr
  Register #(.width(1)) DE_EX_JALR (.D(decode_1_jalr), .clk(clk), .Q(DE_EX_JALR_q));  // open: en, clr
  Register #(.width(1)) DE_EX_eq (.D(decode_1_eq), .clk(clk), .Q(DE_EX_eq_q));  // open: en, clr
  Register #(.width(1)) DE_EX_posRel (.D(decode_1_posrel), .clk(clk), .Q(DE_EX_posRel_q));  // open: en, clr
  Register #(.width(1)) jump (.D(decode_1_jump), .clk(clk), .Q(jump_q));  // open: en, clr
  Register #(.width(1)) store_DX (.D(multiplexer_5_out), .clk(clk), .Q(store_DX_q));  // open: en, clr
  Register #(.width(1)) word_op_DX (.D(decode_1_word_op), .clk(clk), .Q(word_op_DX_q));  // open: en, clr
  Register #(.width(1)) lb_DX (.D(decode_1_lb), .clk(clk), .Q(lb_DX_q));  // open: en, clr
  Register #(.width(32)) DE_EX_PC (.D(PC_q), .clk(clk), .Q(DE_EX_PC_q));  // open: en, clr
  Register #(.width(32)) DE_EX_PCn4 (.D(PCn4_q), .clk(clk), .Q(DE_EX_PCn4_q));  // open: en, clr
  // Bypass_Black_Box bypass_black_box_1: pin names not known; wires that end beside it: rs1_q, rs2_q, bypass_black_box_1_p3, bypass_black_box_1_p4, registerfile_1_p3, registerfile_1_p4, bypass_black_box_1_p7, bypass_black_box_1_p8
  MUX3to1 mux3to1_1 (
    .EX(DE_EX_A_q), .out_5(mux3to1_1_out_5), .WB(registerfile_1_p1), .ME(EX_M_Result_q),
    .Sel(bypass_black_box_1_p7));
  MUX3to1 mux3to1_2 (
    .EX(DE_EX_B_q), .out_5(mux3to1_2_out_5), .WB(registerfile_1_p1), .ME(EX_M_Result_q),
    .Sel(bypass_black_box_1_p8));
  Multiplexer #(.width(32), .enable("false")) multiplexer_6 (
    .in0(mux3to1_2_out_5), .in1(DE_EX_imm_q), .out(multiplexer_6_out), .sel(and_2_out));
  and and_2 (and_2_out, DE_EX_useImm_q, not_7_out);
  not not_7 (not_7_out, DE_EX_branch_q);
  // Comparator_Black_Box comparator_black_box_1: pin names not known; wires that end beside it: mux3to1_1_out_5, multiplexer_6_out, set_signed_q, comparator_black_box_1_p4, comparator_black_box_1_p5
  Multiplexer #(.enable("false")) multiplexer_7 (
    .in0(comparator_black_box_1_p5), .in1(comparator_black_box_1_p4), .out(multiplexer_7_out),
    .sel(DE_EX_eq_q));
  Execute execute_1 (
    .A(mux3to1_1_out_5), .B(mux3to1_2_out_5), .rB(rs2_q), .imm(DE_EX_imm_q), .useImm(DE_EX_useImm_q),
    .ALUop(DE_EX_ALUop_q), .shiftbyregval(DE_EX_shiftreg_q), .UsePCasA(DE_EX_usePCasA_q), .PC(DE_EX_PC_q),
    .JALR(DE_EX_JALR_q), .result(execute_1_result));
  assign bit_extender_2_out = {{31{1'b0}}, comparator_black_box_1_p5};  // Bit_Extender bit_extender_2
  and and_3 (and_3_out, DE_EX_branch_q, xnor_1_out);
  xnor xnor_1 (xnor_1_out, multiplexer_7_out, DE_EX_posRel_q);
  Multiplexer #(.width(32), .enable("false")) multiplexer_8 (
    .in0(execute_1_result), .in1(bit_extender_2_out), .out(multiplexer_8_out), .sel(DE_EX_set_q));
  Multiplexer #(.width(32), .enable("false")) multiplexer_9 (
    .in0(multiplexer_8_out), .in1(DE_EX_PCn4_q), .out(multiplexer_9_out), .sel(jump_q));
  Register #(.width(32)) EX_M_Result (.D(multiplexer_9_out), .clk(clk), .Q(EX_M_Result_q));  // open: en, clr
  Register #(.width(5)) EX_M_rd (.D(DE_EX_rd_q), .clk(clk), .Q(bypass_black_box_1_p4));  // open: en, clr
  Register #(.width(32)) EX_M_B (.D(mux3to1_2_out_5), .clk(clk), .Q(EX_M_B_q));  // open: en, clr
  Register #(.width(1)) EX_M_regWE (.D(DE_EX_regWE_q), .clk(clk), .Q(bypass_black_box_1_p3));  // open: en, clr
  Register #(.width(1)) Load_XM (.D(LOAD_DX_q), .clk(clk), .Q(Load_XM_q));  // open: en, clr
  Register #(.width(1)) store_XM (.D(store_DX_q), .clk(clk), .Q(store_XM_q));  // open: en, clr
  Register #(.width(1)) word_op_XM (.D(word_op_DX_q), .clk(clk), .Q(word_op_XM_q));  // open: en, clr
  Register #(.width(1)) lb_XM (.D(lb_DX_q), .clk(clk), .Q(lb_XM_q));  // open: en, clr
  Memory memory_1 (
    .addy(EX_M_Result_q), .D_in(EX_M_B_q), .store(store_XM_q), .word_op(word_op_XM_q), .clk(clk),
    .load(Load_XM_q), .lb(lb_XM_q), .D_out(memory_1_d_out));
  Register #(.width(32)) M_W_Result (.D(EX_M_Result_q), .clk(clk), .Q(M_W_Result_q));  // open: en, clr
  Register #(.width(32)) M_W_Data (.D(memory_1_d_out), .clk(clk), .Q(M_W_Data_q));  // open: en, clr
  Register #(.width(1)) M_W_regWE (.D(bypass_black_box_1_p3), .clk(clk), .Q(registerfile_1_p3));  // open: en, clr
  Register #(.width(5)) M_W_rd (.D(bypass_black_box_1_p4), .clk(clk), .Q(registerfile_1_p4));  // open: en, clr
  Register #(.width(1)) Load_MW (.D(Load_XM_q), .clk(clk), .Q(Load_MW_q));  // open: en, clr
  Multiplexer #(.width(32), .enable("false")) multiplexer_10 (
    .in0(M_W_Result_q), .in1(M_W_Data_q), .out(registerfile_1_p1), .sel(Load_MW_q));

  // Notes on the sheet:
  //   The RISCV Processor Main Circuit
  //   contents of risc_vprogramrom_1 (hex, n*v repeats v):
  //   ### Test File 1 (Basic Tests that cover all Table B Instructions)###  addi x1, x0, 1 # x1=1 addi x2,
  //   x2, 2 # x2=2 jal x9, 8 # Testing JAL,x9=12 addi x2, x2, 1 addi x2, x2, 1 addi x2, x2, 1 #x2=4 slli
  //   x3, x2, 1 #x3=8 jalr x0, x3, 48 # Testing JALR, writing to x0 addi x2, x2, 1 addi x2, x2, 1 addi x2,
  //   x2, 1 addi x2, x2, 1 addi x2, x2, 1 addi x2, x2, 1 # skipping till here addi x2, x2, 1 # x2 stores 5
  //   now jalr x10, x3, 64 # Testing JALR, adding imm to an odd number, x10=64 lb x8, 4(x1) # Skip add x4,
  //   x2, x8 #x4=5 sll x4, x4, x1 #x4=10 jalr x4, x4, 80 #Testing JALR, imm is odd, now x4=80 addi x2, x2,
  //   1 addi x2, x2, 1 addi x2, x2, 1 #x2=6 bne x2, x4, 8 # Testing BNE, branch taken addi x5, x5, 1 addi
  //   x5, x5, 1 addi x5, x5, 1 #x5=2 slli x6, x5, 2 #x6=8 bne x6, x3, 100 # Testing BNE, branch not taken
  //   beq x6, x3, 16 # Testing BEQ, branch taken, consecutive branches addi x7, x7, 1 addi x7, x7, 1 addi
  //   x7, x7, 1 addi x7, x7, 1 #x7=1 beq x7, x2, 36 # Testing BEQ, branch not taken sw x7, 12(x3) beq x7,
  //   x1, 8 # Testing BEQ, branch taken lui x7, 145 addi x7, x7, 10 #x7=11 blt x7, x4, 12 # Testing BLT,
  //   branch taken addi x8, x8, 1 addi x8, x8, 1 addi x8, x8, 1 addi x8, x8, 1 addi x8, x8, 1 #x8=3 blt
  //   x8, x5, 200 # Testing BLT, branch not taken sw x5, 0(x6) sw x8, 4(x4) bge x10, x9, 8 # Testing BGE,
  //   branch taken (greater than) addi x11, x11, 2 addi x11, x11, 3 addi x11, x11, 4 addi x11, x11, 5 bge
  //   x3, x6, 12 # Testing BGE, branch taken (equal to) addi x12, x12, 5 addi x12, x12, 5 addi x12, x12, 5
  //   addi x12, x12, 5 addi x12, x12, 5 addi x12, x12, 5 BLTU x3, x6, 20 # Testing BLTU, branch not taken
  //   (equal to) addi x13, x0, 12 BLTU x13, x8, 100 # Testing BLTU, branch not taken (not less than) BLTU
  //   x13, x10, 8 # Testing BLTU, branch not taken (not less than) addi x14, x0, 999 addi x14, x14, 9 BGEU
  //   x14, x4, 200 # Testing BGEU, branch not taken auipc x6, 180 sw x9, 16(x0) lw x16, 4(x13) # Load use
  //   Hazard lw x16, 4(x2) # Hazard BGEU x16, x1, 8 # Testing BGEU, branch taken (greater than) addi x17,
  //   x17, 3 addi x17, x17, 3 addi x17, x17, 3 addi x17, x17, 3 BGEU x11, x13, 8 # Testing BGEU, branch
  //   taken (equal) addi x18, x18, 1 addi x18, x18, 1 addi x18, x18, 1 addi x18, x18, 1 addi x18, x18, 1
  //   nop addi x19, x0, -10 addi x20, x0, -11 BLT x19, x20, 28 # Testing BLT with negative numbers, branch
  //   not taken lw x21, 4(x13) lw x22, 4(x2) BLTU x19, x20, 8 # Testing BLTU, branch taken addi x23, x23,
  //   1 addi x23, x23, 1 addi x23, x23, 1 addi x23, x23, 1 BGEU x19, x20, 100 # Testing BGEU with negative
  //   numbers, branch not taken BGE x19, x20, 8 # Testing BGE, branch taken addi x24, x0, 7 addi x24, x0,
  //   7 addi x24, x0, 7
endmodule

module Increment_PC (
  input  [31:0] in_1,
  output [31:0] out_2
);

  // Incrementer #(.width(30)) incrementer_1: pin names not known; wires that end beside it: in_1[31:2], out_2[31:2]

  assign out_2[1:0] = in_1[1:0];

  // Notes on the sheet:
  //   Circuit Incrementing PC
endmodule

module Decode (
  input  [31:0] instr,
  input  [31:0] nop,
  input  zap,
  input  stall,
  output [4:0] rs1,
  output [4:0] rs2,
  output [4:0] rd,
  output [31:0] imm,
  output useImm,
  output [3:0] ALUop,
  output regWE,
  output set,
  output shiftbyregval,
  output setsign,
  output UsePCasA,
  output [31:0] ZeroOutA,
  output load,
  output branch,
  output JALR,
  output eq,
  output posRel,
  output jump,
  output store,
  output word_op,
  output lb
);

  wire decode_black_box_1_p6, not_2_out, or_1_out, or_5_out, or_6_out, or_7_out, or_9_out, or_12_out,
       undriven;
  wire [0:0] not_1_out;
  wire [2:2] not_3_out;
  wire [3:0] decode_black_box_1_p7;
  wire [31:0] bit_extender_2_out, bit_extender_3_out, bit_extender_4_out, bit_extender_5_out,
       decode_black_box_1_p5, decode_black_box_1_p8, multiplexer_1_out, multiplexer_2_out, multiplexer_3_out,
       multiplexer_4_out;

  Multiplexer #(.width(32), .enable("false")) multiplexer_1 (
    .in0(instr), .in1(nop), .out(multiplexer_1_out), .sel(zap));
  // Decode_Black_Box decode_black_box_1: pin names not known; wires that end beside it: multiplexer_1_out, rs1, rs2, rd, decode_black_box_1_p5, decode_black_box_1_p6, decode_black_box_1_p7, decode_black_box_1_p8[0], decode_black_box_1_p8[1], decode_black_box_1_p8[2], decode_black_box_1_p8[3], decode_black_box_1_p8[4], decode_black_box_1_p8[5], decode_black_box_1_p8[6], decode_black_box_1_p8[7], decode_black_box_1_p8[8], decode_black_box_1_p8[9], decode_black_box_1_p8[10], decode_black_box_1_p8[11], decode_black_box_1_p8[12], decode_black_box_1_p8[13], decode_black_box_1_p8[14], decode_black_box_1_p8[15], decode_black_box_1_p8[16], decode_black_box_1_p8[17], decode_black_box_1_p8[18], decode_black_box_1_p8[19], decode_black_box_1_p8[20], decode_black_box_1_p8[21], decode_black_box_1_p8[22], decode_black_box_1_p8[23], decode_black_box_1_p8[24], JALR, decode_black_box_1_p8[26], decode_black_box_1_p8[27], decode_black_box_1_p8[28], decode_black_box_1_p8[29], decode_black_box_1_p8[30]
  or or_1 (or_1_out, multiplexer_1_out[4], ~multiplexer_1_out[5]);  // OR_Gate
  not not_1 (not_1_out[0], multiplexer_1_out[0]);
  not not_2 (not_2_out, decode_black_box_1_p8[20]);
  assign ZeroOutA = {{31{not_2_out}}, not_2_out};  // Bit_Extender bit_extender_1
  or or_2 (set, decode_black_box_1_p8[13], decode_black_box_1_p8[12], decode_black_box_1_p8[11], decode_black_box_1_p8[10]);
  assign bit_extender_2_out = {{19{multiplexer_1_out[31]}}, {multiplexer_1_out[31], multiplexer_1_out[7], multiplexer_1_out[30:25], multiplexer_1_out[11:8], not_1_out[0]}};  // Bit_Extender bit_extender_2
  assign bit_extender_3_out = {{20{multiplexer_1_out[31]}}, {multiplexer_1_out[31:25], multiplexer_1_out[11:7]}};  // Bit_Extender bit_extender_3
  assign bit_extender_4_out = {{11{multiplexer_1_out[31]}}, {multiplexer_1_out[31], multiplexer_1_out[19:12], multiplexer_1_out[20], multiplexer_1_out[30:21], not_1_out[0]}};  // Bit_Extender bit_extender_4
  assign bit_extender_5_out = {{20{multiplexer_1_out[31]}}, multiplexer_1_out[31:20]};  // Bit_Extender bit_extender_5
  not not_3 (not_3_out[2], multiplexer_1_out[0]);
  or or_3 (setsign, decode_black_box_1_p8[11], decode_black_box_1_p8[10], decode_black_box_1_p8[29], decode_black_box_1_p8[28]);
  or or_4 (shiftbyregval, decode_black_box_1_p8[14], decode_black_box_1_p8[16], decode_black_box_1_p8[18]);
  or or_5 (or_5_out, decode_black_box_1_p8[31], decode_black_box_1_p8[29], decode_black_box_1_p8[28], decode_black_box_1_p8[27], decode_black_box_1_p8[26], decode_black_box_1_p8[30]);
  Multiplexer #(.width(32), .enable("false")) multiplexer_2 (
    .in0(bit_extender_5_out), .in1(bit_extender_3_out), .out(multiplexer_2_out), .sel(or_7_out));
  or or_6 (or_6_out, undriven, lb, JALR, decode_black_box_1_p8[22], decode_black_box_1_p8[23]);
  or or_7 (or_7_out, undriven, decode_black_box_1_p8[23]);
  or or_8 (UsePCasA, decode_black_box_1_p8[21], or_5_out, decode_black_box_1_p8[24]);
  Multiplexer #(.width(32), .enable("false")) multiplexer_3 (
    .in0(bit_extender_2_out), .in1(multiplexer_2_out), .out(multiplexer_3_out), .sel(or_6_out));
  Multiplexer #(.width(32), .enable("false")) multiplexer_4 (
    .in0(multiplexer_3_out), .in1(bit_extender_4_out), .out(multiplexer_4_out),
    .sel(decode_black_box_1_p8[24]));
  or or_9 (or_9_out, decode_black_box_1_p8[22], decode_black_box_1_p8[23], decode_black_box_1_p8[24], JALR, decode_black_box_1_p8[26], decode_black_box_1_p8[27], decode_black_box_1_p8[28], decode_black_box_1_p8[29], decode_black_box_1_p8[30], decode_black_box_1_p8[31], lb, undriven);
  or or_10 (eq, decode_black_box_1_p8[27], decode_black_box_1_p8[26]);
  or or_11 (posRel, decode_black_box_1_p8[26], decode_black_box_1_p8[28], decode_black_box_1_p8[30]);
  or or_12 (or_12_out, JALR, decode_black_box_1_p8[24]);
  or or_13 (store, decode_black_box_1_p8[23], undriven);
  Multiplexer #(.enable("false")) multiplexer_5 (
    .in0(decode_black_box_1_p6), .in1(multiplexer_1_out[0]), .out(useImm), .sel(or_9_out));
  Multiplexer #(.width(4), .enable("false")) multiplexer_6 (
    .in0(decode_black_box_1_p7), .in1({multiplexer_1_out[0], {3{not_3_out[2]}}}), .out(ALUop), .sel(or_9_out));
  or or_14 (load, decode_black_box_1_p8[22], lb);
  or or_15 (word_op, decode_black_box_1_p8[22], decode_black_box_1_p8[23]);
  or or_16 (regWE, or_1_out, or_12_out);
  Multiplexer #(.width(32), .enable("false")) multiplexer_7 (
    .in0(decode_black_box_1_p5), .in1(multiplexer_4_out), .out(imm), .sel(or_9_out));
  and and_1 (branch, or_5_out, ~stall);  // AND_Gate
  and and_2 (jump, or_12_out, ~stall);  // AND_Gate

  // Notes on the sheet:
  //   The Decode Circuit
endmodule

module Execute (
  input  [31:0] A,
  input  [31:0] B,
  input  [4:0] rB,
  input  [31:0] imm,
  input  useImm,
  input  [3:0] ALUop,
  input  shiftbyregval,
  input  UsePCasA,
  input  [31:0] PC,
  input  JALR,
  output [31:0] result
);

  wire not_1_out;
  wire [0:0] alu_1_p5;
  wire [4:0] multiplexer_3_out;
  wire [31:0] multiplexer_1_out, multiplexer_2_out, multiplexer_4_out;

  not not_1 (not_1_out, JALR);
  Multiplexer #(.width(32), .enable("false")) multiplexer_1 (.in0(B), .in1(imm), .out(multiplexer_1_out), .sel(useImm));
  Multiplexer #(.width(32), .enable("false")) multiplexer_2 (
    .in0(multiplexer_1_out), .in1(A), .out(multiplexer_2_out), .sel(shiftbyregval));
  Multiplexer #(.width(5), .enable("false")) multiplexer_3 (
    .in0(rB), .in1(B[4:0]), .out(multiplexer_3_out), .sel(shiftbyregval));
  Multiplexer #(.width(32), .enable("false")) multiplexer_4 (
    .in0(A), .in1(PC), .out(multiplexer_4_out), .sel(UsePCasA));
  // ALU alu_1: pin names not known; wires that end beside it: multiplexer_4_out, multiplexer_2_out, ALUop, multiplexer_3_out, {result[31:1], alu_1_p5[0]}
  and and_1 (result[0], not_1_out, alu_1_p5[0]);

  // Notes on the sheet:
  //   The Execute Circuit
endmodule

module MUX3to1 (
  input  [1:0] Sel,
  input  [31:0] EX,
  input  [31:0] WB,
  input  [31:0] ME,
  output [31:0] out_5
);

  wire [31:0] multiplexer_1_out;

  Multiplexer #(.width(32), .enable("false")) multiplexer_1 (.in0(EX), .in1(WB), .out(multiplexer_1_out), .sel(Sel[0]));
  Multiplexer #(.width(32), .enable("false")) multiplexer_2 (
    .in0(multiplexer_1_out), .in1(ME), .out(out_5), .sel(Sel[1]));

  // Notes on the sheet:
  //   3-1 Mux Circuit
endmodule

module Memory (
  input  [31:0] addy,
  input  [31:0] D_in,
  input  store,
  input  word_op,
  input  clk,
  input  load,
  input  lb,
  output [31:0] D_out
);

  wire not_1_out;
  wire [3:0] sel_byte_1_sel_byte;
  wire [7:0] multiplexer_2_out;
  wire [23:0] bit_extender_1_out;
  wire [31:0] bit_extender_2_out, multiplexer_1_out, ram_1_p7;

  Multiplexer #(.width(32), .enable("false")) multiplexer_1 (
    .in0(D_in), .in1({D_in[7:0], D_in[7:0], D_in[7:0], D_in[7:0]}), .out(multiplexer_1_out), .sel(not_1_out));
  not not_1 (not_1_out, word_op);
  assign bit_extender_1_out = {{2{addy[23]}}, addy[23:2]};  // Bit_Extender bit_extender_1
  sel_byte sel_byte_1 (.A(addy[1:0]), .word_op(word_op), .sel_Byte(sel_byte_1_sel_byte));
  // RAM #(.addrWidth(24)) ram_1: pin names not known; wires that end beside it: bit_extender_1_out, multiplexer_1_out, store, sel_byte_1_sel_byte, clk, load, ram_1_p7
  Multiplexer #(.select(2), .width(8), .enable("false")) multiplexer_2 (
    .in0(ram_1_p7[7:0]), .in1(ram_1_p7[15:8]), .in2(ram_1_p7[23:16]), .in3(ram_1_p7[31:24]),
    .out(multiplexer_2_out), .sel(addy[1:0]));
  assign bit_extender_2_out = {{24{multiplexer_2_out[7]}}, multiplexer_2_out};  // Bit_Extender bit_extender_2
  Multiplexer #(.width(32), .enable("false")) multiplexer_3 (
    .in0(ram_1_p7), .in1(bit_extender_2_out), .out(D_out), .sel(lb));

  // Notes on the sheet:
  //   The Memory Circuit
endmodule

module sel_byte (
  input  [1:0] A,
  input  word_op,
  output [3:0] sel_Byte
);

  wire [3:0] and_1_out, bit_extender_1_out;

  assign bit_extender_1_out = {{3{word_op}}, word_op};  // Bit_Extender bit_extender_1
  and and_1 (and_1_out[0], ~A[0], ~A[1]);  // AND_Gate
  and and_2 (and_1_out[1], A[0], ~A[1]);  // AND_Gate
  and and_3 (and_1_out[2], ~A[0], A[1]);  // AND_Gate
  and and_4 (and_1_out[3], A[0], A[1]);
  Multiplexer #(.width(4), .enable("false")) multiplexer_1 (
    .in0(and_1_out), .in1(bit_extender_1_out), .out(sel_Byte), .sel(word_op));

  // Notes on the sheet:
  //   The Select-Byte Circuit
endmodule

module LoadUseDetection (
  input  [4:0] rs1_FD,
  input  [4:0] rs2_FD,
  input  [4:0] rd_DX,
  input  load_DX,
  output stall
);

  wire and_1_out, and_2_out, or_1_out, or_2_out;
  wire [4:0] not_1_out, not_2_out, xor_1_out, xor_2_out;

  assign xor_1_out = rs2_FD ^ rd_DX;  // XOR_Gate xor_1, 5 bits wide
  assign xor_2_out = rs1_FD ^ rd_DX;  // XOR_Gate xor_2, 5 bits wide
  assign not_1_out = ~xor_2_out;  // NOT_Gate not_1, 5 bits wide
  assign not_2_out = ~xor_1_out;  // NOT_Gate not_2, 5 bits wide
  and and_1 (and_1_out, not_1_out[0], not_1_out[1], not_1_out[2], not_1_out[3], not_1_out[4]);
  and and_2 (and_2_out, not_2_out[0], not_2_out[1], not_2_out[2], not_2_out[3], not_2_out[4]);
  or or_1 (or_1_out, rd_DX[0], rd_DX[1], rd_DX[2], rd_DX[3], rd_DX[4]);
  or or_2 (or_2_out, and_1_out, and_2_out);
  and and_3 (stall, or_2_out, or_1_out, load_DX);

  // Notes on the sheet:
  //   Load-Use Detection Circuit
endmodule

module Flush (
  input  jump,
  output [31:0] nop
);

  not not_1 (nop[3], jump);
  assign nop[31:5] = {{26{1'b0}}, nop[3]};  // Bit_Extender bit_extender_1

  assign {nop[4], nop[2:0]} = {jump, nop[3], {2{jump}}};

  // Notes on the sheet:
  //   The Flush Circuit
endmodule
